# Fritzing sketch Electronics Diagram (saved by Fritzing 0.8.5b)
stripboards: 1

parts:
  Part1 = Arduino Nano (Rev3.0)
  Part2 = Adafruit FONA - Mini Cellular GSM Breakout
  U1 = LIPO-2000mAh [package=lipo-2000]  # not connected

nets:
  N1: Part1.D2, Part2.RXD_5V
  N2: Part1.D3, Part2.TXD_5V
  N3: Part1.D4, Part2.PWRKEY_5V
  N4: Part1.D5, Part2.RESET_5V
  N5: Part1.D6, Part2.PWRSTAT_5V
  N6: Part1.VIN, Part2.VCCIO, Part2.VBAT
  GND: Part1.GND, Part2.GND

notes:
  The Prototype use 1200 mAh 3.7 Battery
  This represents the older Fona model.

custom parts:
  Adafruit FONA - Mini Cellular GSM Breakout: An all-in-one cellular phone module that lets you add voice, text, SMS and GPRS data to your project. Quad-band 850/900/1800/1900MHz - connect onto any global GSM network with any 2G SIM. Includes an onboard LiPoly battery charging circuitry so you can take your project on the go. Also works as an FM radio receiver.
